# Fritzing sketch remoteIR (saved by Fritzing 0.8.5b)
breadboards: 1

parts:
  Q1 = NPN-Transistor [package="SOT-23 [SMD]"]
  LED2 = LED - 5mm [color="Infrared (880nm)" package="5 mm [THT]"]
  Pi1 = Adafruit Pi Cobbler
  R2 = Resistor [tolerance=±5% resistance=10 package=THT]
  R1 = Resistor [tolerance=±5% resistance=47 package=THT]
  Part1 = Arduino Uno (Rev3)

nets:
  GND: Q1.2, Pi1.GND, Part1.GND
  N1: Q1.0, R1.Pin_1
  N2: Q1.1, R2.Pin_1
  N3: LED2.cathode, R2.Pin_0
  N4: LED2.anode, Pi1.5V0, Part1.5V
  N5: Pi1.MOSI, Part1.D11_PWM/MOSI
  N6: Pi1.MISO, Part1.D12/MISO
  N7: Pi1.SCLK, Part1.D13/SCK
  N8: Pi1.CE0, Part1.D10_PWM/SS
  N9: R1.Pin_0, Part1.D3_PWM

custom parts:
  Adafruit Pi Cobbler: Adafruit Pi Cobbler GPIO Breakout for Raspberry Pi
